# Fritzing sketch ACT2-LEDARDUINO (saved by Fritzing 0.9.9b)
breadboards: 1

parts:
  Componente1 = Arduino Nano (Rev3.0) (ICSP)
  LED1 = smd LED [color="Red (633nm)" package="0805 [SMD]"]
  R1 = Resistor [tolerance=±5% resistance=220 package="2512 [SMD]"]

nets:
  N1: Componente1.GND, LED1.cathode
  N2: Componente1.D9, R1.Pin_1
  N3: LED1.anode, R1.Pin_0
