# Fritzing sketch ACT3-SWPULLDOWN (saved by Fritzing 0.9.9b)
breadboards: 1

parts:
  Componente1 = Arduino Nano (Rev3.0) (ICSP)
  LED1 = smd LED [color="Red (633nm)" package="0805 [SMD]"]
  R1 = Resistor [tolerance=±5% resistance=220 package="2512 [SMD]"]
  S1 = Pushbutton [package="[THT]"]
  R2 = Resistor [tolerance=±5% resistance=1k package="2512 [SMD]"]

nets:
  N1: Componente1.GND, LED1.cathode, R2.Pin_1
  N2: Componente1.D9, R1.Pin_1
  N3: Componente1.D10, S1.Pin_3, S1.Pin_4, R2.Pin_0
  N4: Componente1.5V, S1.Pin_1, S1.Pin_2
  N5: LED1.anode, R1.Pin_0
