# Fritzing sketch Circuito_serie (saved by Fritzing 0.9.9b)
breadboards: 1

parts:
  5V = Battery Holders [package=battery-aaa]
  R1 = Resistor [tolerance=±5% power=0.25 resistance=220 package=THT]
  R2 = Resistor [tolerance=±5% power=0.25 resistance=220 package=THT]
  R3 = Resistor [tolerance=±5% power=0.25 resistance=100 package=THT]

nets:
  N1: 5V.-, R3.Pin_1
  N2: 5V.+, R1.Pin_0
  N3: R1.Pin_1, R2.Pin_0
  N4: R2.Pin_1, R3.Pin_0
