# Fritzing sketch Fuente_Alimentacion (saved by Fritzing 0.9.9b)
breadboards: 1

parts:
  D1 = Rectifier Diode [part_number=1N4001 package="Melf DO-213 AB [SMD]"]
  D2 = Rectifier Diode [part_number=1N4001 package="Melf DO-213 AB [SMD]"]
  D3 = Rectifier Diode [part_number=1N4001 package="Melf DO-213 AB [SMD]"]
  D4 = Rectifier Diode [part_number=1N4001 package="Melf DO-213 AB [SMD]"]
  C1 = Electrolytic Capacitor [capacitance=10μF voltage=35V package="0605 [SMD, electrolytic]"]
  IC1 = Voltage Regulator [package=to220-igo]
  C2 = Capacitor [package=cap-pth-small2]
  C3 = Capacitor [package=cap-pth-small2]

nets:
  N1: D1.cathode, D2.anode
  N2: D1.anode, D3.anode, C1.+, IC1.IN, C2.2, C3.2
  N3: D2.cathode, D4.cathode, C1.-, IC1.GND, C2.1
  N4: D3.cathode, D4.anode
  N5: IC1.OUT, C3.1
